# Fritzing sketch 4n35 (saved by Fritzing 0.9.3b)
breadboards: 1

parts:
  R2 = Resistor [tolerance=±5% resistance=220 package=THT]
  R1 = Resistor [tolerance=±5% resistance=1k package=THT]
  LED1 = LED - 5mm [color="Red (633nm)" package="5 mm [THT]"]
  U1 = 4N35 [package=THT]
  Raspberry_Pi_2 = Raspberry Pi 3 [part_number=RPI-3-V1.2]

nets:
  N1: R2.Pin_0, R1.Pin_0, Raspberry_Pi_2.3v3
  N2: R2.Pin_1, LED1.anode
  N3: R1.Pin_1, U1.Pin_1
  N4: LED1.cathode, U1.Pin_5
  N5: U1.Pin_2, Raspberry_Pi_2.GPIO17
  N6: U1.Pin_4, Raspberry_Pi_2.GND

custom parts:
  4N35: Optocoupler - keeps you from frying your stuff!
  Raspberry Pi 3: The RPi3, a faster version of the awesome Raspberry Pi 2 B ARM Board with 40 pin gpio. Ready for special Raspberry Pi B+ and RPi2 Hat (Hardware attached (on) top)
