# Fritzing sketch 74HC595 (saved by Fritzing 0.9.3b)
breadboards: 1

parts:
  IC2 = IC, DIP package, 16 pins [chip_label=74HC595]
  R4 = Resistor [tolerance=±5% resistance=220 package=THT]
  LED1 = LED - 5mm [color="Red (633nm)" package="5 mm [THT]"]
  LED2 = LED - 5mm [color="Green (560nm)" package="5 mm [THT]"]
  LED3 = LED - 5mm [color="Yellow (595nm)" package="5 mm [THT]"]
  LED4 = LED - 5mm [color="Blue (470nm)" package="5 mm [THT]"]
  LED5 = LED - 5mm [color="Red (633nm)" package="5 mm [THT]"]
  LED6 = LED - 5mm [color="Green (565nm)" package="5 mm [THT]"]
  LED7 = LED - 5mm [color="Yellow (595nm)" package="5 mm [THT]"]
  LED8 = LED - 5mm [color="Blue (470nm)" package="5 mm [THT]"]
  R5 = Resistor [tolerance=±5% resistance=220 package=THT]
  R6 = Resistor [tolerance=±5% resistance=220 package=THT]
  R7 = Resistor [tolerance=±5% resistance=220 package=THT]
  R8 = Resistor [tolerance=±5% resistance=220 package=THT]
  R9 = Resistor [tolerance=±5% resistance=220 package=THT]
  R10 = Resistor [tolerance=±5% resistance=220 package=THT]
  R11 = Resistor [tolerance=±5% resistance=220 package=THT]
  Raspberry_Pi_2 = Raspberry Pi 3 [part_number=RPI-3-V1.2]

nets:
  N1: IC2.pin1, R5.Pin_1
  N2: IC2.pin2, R6.Pin_1
  N3: IC2.pin3, R7.Pin_1
  N4: IC2.pin4, R8.Pin_1
  N5: IC2.pin5, R9.Pin_1
  N6: IC2.pin6, R10.Pin_1
  N7: IC2.pin7, R11.Pin_1
  N8: IC2.pin8, IC2.pin13, LED1.cathode, LED2.cathode, LED3.cathode, LED4.cathode, LED5.cathode, LED6.cathode, LED7.cathode, LED8.cathode, Raspberry_Pi_2.GND
  N9: IC2.pin10, IC2.pin16, Raspberry_Pi_2.3v3
  N10: IC2.pin11, Raspberry_Pi_2.GPIO27
  N11: IC2.pin12, Raspberry_Pi_2.GPIO18
  N12: IC2.pin14, Raspberry_Pi_2.GPIO17
  N13: IC2.pin15, R4.Pin_1
  N14: R4.Pin_0, LED1.anode
  N15: LED2.anode, R5.Pin_0
  N16: LED3.anode, R6.Pin_0
  N17: LED4.anode, R7.Pin_0
  N18: LED5.anode, R8.Pin_0
  N19: LED6.anode, R9.Pin_0
  N20: LED7.anode, R10.Pin_0
  N21: LED8.anode, R11.Pin_0

custom parts:
  Raspberry Pi 3: The RPi3, a faster version of the awesome Raspberry Pi 2 B ARM Board with 40 pin gpio. Ready for special Raspberry Pi B+ and RPi2 Hat (Hardware attached (on) top)
