# Fritzing sketch AnswerMachine (saved by Fritzing 0.9.3b)
breadboards: 1

parts:
  LED1 = LED - 5mm [color="Blue (430nm)" package="5 mm [THT]"]
  LED2 = LED - 5mm [color="Yellow (595nm)" package="5 mm [THT]"]
  LED3 = LED - 5mm [color="Green (560nm)" package="5 mm [THT]"]
  S1 = Pushbutton [package="[THT]"]
  S2 = Pushbutton [package="[THT]"]
  R1 = Resistor [tolerance=±5% resistance=220 package=THT]
  R2 = Resistor [tolerance=±5% resistance=220 package=THT]
  R3 = Resistor [tolerance=±5% resistance=220 package=THT]
  R4 = Resistor [tolerance=±5% resistance=10k package=THT]
  R5 = Resistor [tolerance=±5% resistance=10k package=THT]
  S3 = Pushbutton [package="[THT]"]
  R6 = Resistor [tolerance=±5% resistance=10k package=THT]
  LED4 = LED - 5mm [color="Red (633nm)" package="5 mm [THT]"]
  S4 = Pushbutton [package="[THT]"]
  R7 = Resistor [tolerance=±5% resistance=10k package=THT]
  R8 = Resistor [tolerance=±5% resistance=220 package=THT]
  S5 = buzzer [package="[THT]"]
  Q1 = NPN-Transistor [package="TO92 [THT]"]
  R9 = Resistor [tolerance=±5% resistance=1k package=THT]
  Raspberry_Pi_2 = Raspberry Pi 3 [part_number=RPI-3-V1.2]

nets:
  N1: LED1.cathode, LED2.cathode, LED3.cathode, R4.Pin_0, R5.Pin_0, R6.Pin_0, LED4.cathode, R7.Pin_0, Q1.E, Raspberry_Pi_2.GND
  N2: LED1.anode, R1.Pin_0
  N3: LED2.anode, R2.Pin_0
  N4: LED3.anode, R3.Pin_0
  VCC: S1.Pin_1, S1.Pin_2, S2.Pin_1, S2.Pin_2, S3.Pin_1, S3.Pin_2, S4.Pin_1, S4.Pin_2, S5.VCC, Raspberry_Pi_2.5V
  N5: S1.Pin_3, S1.Pin_4, R4.Pin_1, Raspberry_Pi_2.GPIO27
  N6: S2.Pin_3, S2.Pin_4, R5.Pin_1, Raspberry_Pi_2.GPIO22
  N7: R1.Pin_1, Raspberry_Pi_2.GPIO6
  N8: R2.Pin_1, Raspberry_Pi_2.GPIO13
  N9: R3.Pin_1, Raspberry_Pi_2.GPIO19
  N10: S3.Pin_3, S3.Pin_4, R6.Pin_1, Raspberry_Pi_2.GPIO23
  N11: LED4.anode, R8.Pin_0
  N12: S4.Pin_3, S4.Pin_4, R7.Pin_1, Raspberry_Pi_2.GPIO18
  N13: R8.Pin_1, Raspberry_Pi_2.GPIO5
  N14: S5.GND, Q1.C
  N15: Q1.B, R9.Pin_0
  N16: R9.Pin_1, Raspberry_Pi_2.GPIO17

custom parts:
  Raspberry Pi 3: The RPi3, a faster version of the awesome Raspberry Pi 2 B ARM Board with 40 pin gpio. Ready for special Raspberry Pi B+ and RPi2 Hat (Hardware attached (on) top)
