# Fritzing sketch Button (saved by Fritzing 0.9.3b)
breadboards: 1

parts:
  R1 = Resistor [tolerance=±5% resistance=10k package=THT]
  S1 = Momentary Switch [package=ksa_sealed_tac_switch]
  LED1 = LED - 5mm [color="Red (633nm)" package="5 mm [THT]"]
  R2 = Resistor [tolerance=±5% resistance=220 package=THT]
  Raspberry_Pi_2 = Raspberry Pi 3 [part_number=RPI-3-V1.2]

nets:
  N1: R1.Pin_0, S1.2, Raspberry_Pi_2.GPIO12
  N2: R1.Pin_1, Raspberry_Pi_2.GND
  N3: S1.4, Raspberry_Pi_2.3V3
  N4: LED1.anode, R2.Pin_0
  N5: R2.Pin_1, Raspberry_Pi_2.GPIO17

custom parts:
  Raspberry Pi 3: The RPi3, a faster version of the awesome Raspberry Pi 2 B ARM Board with 40 pin gpio. Ready for special Raspberry Pi B+ and RPi2 Hat (Hardware attached (on) top)
