# Fritzing sketch ButtonPiano (saved by Fritzing 0.9.3b)
breadboards: 1

parts:
  S1 = buzzer [package="[THT]"]
  Q1 = NPN-Transistor [package="TO92 [THT]"]
  R1 = Resistor [tolerance=±5% resistance=1k package=THT]
  S2 = Pushbutton [package="[THT]"]
  S3 = Pushbutton [package="[THT]"]
  S4 = Pushbutton [package="[THT]"]
  S5 = Pushbutton [package="[THT]"]
  S6 = Pushbutton [package="[THT]"]
  S7 = Pushbutton [package="[THT]"]
  S8 = Pushbutton [package="[THT]"]
  R2 = Resistor [tolerance=±5% resistance=10k package=THT]
  R3 = Resistor [tolerance=±5% resistance=10k package=THT]
  R4 = Resistor [tolerance=±5% resistance=10k package=THT]
  R5 = Resistor [tolerance=±5% resistance=10k package=THT]
  R6 = Resistor [tolerance=±5% resistance=10k package=THT]
  R7 = Resistor [tolerance=±5% resistance=10k package=THT]
  R8 = Resistor [tolerance=±5% resistance=10k package=THT]
  Raspberry_Pi_2 = Raspberry Pi 3 [part_number=RPI-3-V1.2]

nets:
  N1: S1.GND, Q1.C
  VCC: S1.VCC, S2.Pin_1, S2.Pin_2, S3.Pin_1, S3.Pin_2, S4.Pin_1, S4.Pin_2, S5.Pin_1, S5.Pin_2, S6.Pin_1, S6.Pin_2, S7.Pin_1, S7.Pin_2, S8.Pin_1, S8.Pin_2, Raspberry_Pi_2.5V
  N2: Q1.E, R2.Pin_0, R3.Pin_0, R4.Pin_0, R5.Pin_0, R6.Pin_0, R7.Pin_0, R8.Pin_0, Raspberry_Pi_2.GND
  N3: Q1.B, R1.Pin_0
  N4: R1.Pin_1, Raspberry_Pi_2.GPIO17
  N5: S2.Pin_3, S2.Pin_4, R2.Pin_1, Raspberry_Pi_2.GPIO27
  N6: S3.Pin_3, S3.Pin_4, R3.Pin_1, Raspberry_Pi_2.GPIO22
  N7: S4.Pin_3, S4.Pin_4, R4.Pin_1, Raspberry_Pi_2.GPIO23
  N8: S5.Pin_3, S5.Pin_4, R5.Pin_1, Raspberry_Pi_2.GPIO24
  N9: S6.Pin_3, S6.Pin_4, R6.Pin_1, Raspberry_Pi_2.GPIO25
  N10: S7.Pin_3, S7.Pin_4, R7.Pin_1, Raspberry_Pi_2.GPIO8
  N11: S8.Pin_3, S8.Pin_4, R8.Pin_1, Raspberry_Pi_2.GPIO7

custom parts:
  Raspberry Pi 3: The RPi3, a faster version of the awesome Raspberry Pi 2 B ARM Board with 40 pin gpio. Ready for special Raspberry Pi B+ and RPi2 Hat (Hardware attached (on) top)
