# Fritzing sketch Flowing LED (saved by Fritzing 0.9.3b)
breadboards: 1

parts:
  LED1 = LED - 5mm [color="Red (633nm)" package="5 mm [THT]"]
  R1 = Resistor [tolerance=±5% resistance=220 package=THT]
  R2 = Resistor [tolerance=±5% resistance=220 package=THT]
  LED2 = LED - 5mm [color="Red (633nm)" package="5 mm [THT]"]
  R3 = Resistor [tolerance=±5% resistance=220 package=THT]
  LED3 = LED - 5mm [color="Red (633nm)" package="5 mm [THT]"]
  R4 = Resistor [tolerance=±5% resistance=220 package=THT]
  LED4 = LED - 5mm [color="Red (633nm)" package="5 mm [THT]"]
  R5 = Resistor [tolerance=±5% resistance=220 package=THT]
  LED5 = LED - 5mm [color="Red (633nm)" package="5 mm [THT]"]
  R6 = Resistor [tolerance=±5% resistance=220 package=THT]
  LED6 = LED - 5mm [color="Red (633nm)" package="5 mm [THT]"]
  R7 = Resistor [tolerance=±5% resistance=220 package=THT]
  LED7 = LED - 5mm [color="Red (633nm)" package="5 mm [THT]"]
  R8 = Resistor [tolerance=±5% resistance=220 package=THT]
  LED8 = LED - 5mm [color="Red (633nm)" package="5 mm [THT]"]
  Raspberry_Pi_2 = Raspberry Pi 3 [part_number=RPI-3-V1.2]

nets:
  N1: LED1.cathode, LED2.cathode, LED3.cathode, LED4.cathode, LED5.cathode, LED6.cathode, LED7.cathode, LED8.cathode, Raspberry_Pi_2.GND
  N2: LED1.anode, R1.Pin_1
  N3: R1.Pin_0, Raspberry_Pi_2.GPIO22
  N4: R2.Pin_0, Raspberry_Pi_2.GPIO23
  N5: R2.Pin_1, LED2.anode
  N6: R3.Pin_0, Raspberry_Pi_2.GPIO24
  N7: R3.Pin_1, LED3.anode
  N8: R4.Pin_0, Raspberry_Pi_2.GPIO25
  N9: R4.Pin_1, LED4.anode
  N10: R5.Pin_0, Raspberry_Pi_2.GPIO8
  N11: R5.Pin_1, LED5.anode
  N12: R6.Pin_0, Raspberry_Pi_2.GPIO27
  N13: R6.Pin_1, LED6.anode
  N14: R7.Pin_0, Raspberry_Pi_2.GPIO18
  N15: R7.Pin_1, LED7.anode
  N16: R8.Pin_0, Raspberry_Pi_2.GPIO17
  N17: R8.Pin_1, LED8.anode

custom parts:
  Raspberry Pi 3: The RPi3, a faster version of the awesome Raspberry Pi 2 B ARM Board with 40 pin gpio. Ready for special Raspberry Pi B+ and RPi2 Hat (Hardware attached (on) top)
