# Fritzing sketch LCD1602 (saved by Fritzing 0.9.3b)
breadboards: 1

parts:
  LCD1 = LCD screen
  R1 = Potentiometer [package=THT]
  Raspberry_Pi_2 = Raspberry Pi 3 [part_number=RPI-3-V1.2]

nets:
  VSS: LCD1.VSS, LCD1.R/W, LCD1.LED-, R1.leg2, Raspberry_Pi_2.GND
  VDD: LCD1.VDD, R1.leg1, Raspberry_Pi_2.5V
  N1: LCD1.V0, R1.wiper
  N2: LCD1.RS, Raspberry_Pi_2.GPIO27
  N3: LCD1.E, Raspberry_Pi_2.GPIO22
  N4: LCD1.DB4, Raspberry_Pi_2.GPIO25
  N5: LCD1.DB5, Raspberry_Pi_2.GPIO24
  N6: LCD1.DB6, Raspberry_Pi_2.GPIO23
  N7: LCD1.DB7, Raspberry_Pi_2.GPIO18
  N8: LCD1.LED+, Raspberry_Pi_2.3v3

custom parts:
  LCD screen: A standard character display, usually with 2x16 characters. Comes in many colors.
  Potentiometer: A standard adjustable resistor (potentiometer).
  Raspberry Pi 3: The RPi3, a faster version of the awesome Raspberry Pi 2 B ARM Board with 40 pin gpio. Ready for special Raspberry Pi B+ and RPi2 Hat (Hardware attached (on) top)
