# Fritzing sketch NE555 (saved by Fritzing 0.9.3b)
breadboards: 1

parts:
  IC1 = IC, DIP package, 8 pins [chip_label=NE555]
  R1 = Potentiometer [package=THT]
  R2 = Resistor [tolerance=±5% resistance=10k package=THT]
  C1 = Capacitor [package=cap-pth-small2]
  C2 = Capacitor [package=cap-pth-small2]
  Raspberry_Pi_2 = Raspberry Pi 3 [part_number=RPI-3-V1.2]

nets:
  N1: IC1.pin1, C1.1, C2.2, Raspberry_Pi_2.GND
  N2: IC1.pin2, IC1.pin6, R1.leg1, C1.2
  N3: IC1.pin3, Raspberry_Pi_2.GPIO18
  N4: IC1.pin4, IC1.pin8, R2.Pin_0, Raspberry_Pi_2.5V
  N5: IC1.pin5, C2.1
  N6: IC1.pin7, R1.wiper, R2.Pin_1

custom parts:
  Potentiometer: A standard adjustable resistor (potentiometer).
  Capacitor: Capacitor Standard 0603 ceramic capacitor, and 0.1 leaded capacitor.
  Raspberry Pi 3: The RPi3, a faster version of the awesome Raspberry Pi 2 B ARM Board with 40 pin gpio. Ready for special Raspberry Pi B+ and RPi2 Hat (Hardware attached (on) top)
