# Fritzing sketch RGB LED (saved by Fritzing 0.9.3b)
breadboards: 1

parts:
  R2 = Resistor [tolerance=±5% resistance=220 package=THT]
  R1 = Resistor [tolerance=±5% resistance=220 package=THT]
  R3 = Resistor [tolerance=±5% resistance=220 package=THT]
  LED1 = RGB LED (com. anode, rbg) [package="5 mm [THT]"]
  Raspberry_Pi_2 = Raspberry Pi 3 [part_number=RPI-3-V1.2]

nets:
  N1: R2.Pin_0, Raspberry_Pi_2.GPIO27
  N2: R2.Pin_1, LED1.green_cathode
  N3: R1.Pin_0, Raspberry_Pi_2.GPIO17
  N4: R1.Pin_1, LED1.red_cathode
  N5: R3.Pin_0, Raspberry_Pi_2.GPIO18
  N6: R3.Pin_1, LED1.blue_cathode
  N7: LED1.common_anode, Raspberry_Pi_2.GND

custom parts:
  Raspberry Pi 3: The RPi3, a faster version of the awesome Raspberry Pi 2 B ARM Board with 40 pin gpio. Ready for special Raspberry Pi B+ and RPi2 Hat (Hardware attached (on) top)
