# Fritzing sketch Servo (saved by Fritzing 0.9.3b)

parts:
  module1 = Servo
  Raspberry_Pi_2 = Raspberry Pi 3 [part_number=RPI-3-V1.2]

nets:
  N1: module1.Brown, Raspberry_Pi_2.GND
  N2: module1.Red, Raspberry_Pi_2.3v3
  N3: module1.Orange, Raspberry_Pi_2.GPIO18

custom parts:
  Servo: servo
  Raspberry Pi 3: The RPi3, a faster version of the awesome Raspberry Pi 2 B ARM Board with 40 pin gpio. Ready for special Raspberry Pi B+ and RPi2 Hat (Hardware attached (on) top)
