# Fritzing sketch Slide switch (saved by Fritzing 0.9.3b)
breadboards: 1

parts:
  R1 = Resistor [tolerance=±5% resistance=220 package=THT]
  LED1 = LED - 5mm [color="Red (633nm)" package="5 mm [THT]"]
  U1 = SWITCH_SPDT [package=kps-1290]
  R2 = Resistor [tolerance=±5% resistance=220 package=THT]
  LED2 = LED - 5mm [color="Green (560nm)" package="5 mm [THT]"]
  Raspberry_Pi_2 = Raspberry Pi 3 [part_number=RPI-3-V1.2]

nets:
  N1: R1.Pin_0, LED1.anode
  N2: R1.Pin_1, Raspberry_Pi_2.GPIO27
  N3: LED1.cathode, U1.S, LED2.cathode, Raspberry_Pi_2.GND
  N4: U1.O, Raspberry_Pi_2.3v3
  N5: U1.P, Raspberry_Pi_2.GPIO17
  N6: R2.Pin_0, LED2.anode
  N7: R2.Pin_1, Raspberry_Pi_2.GPIO22

custom parts:
  Raspberry Pi 3: The RPi3, a faster version of the awesome Raspberry Pi 2 B ARM Board with 40 pin gpio. Ready for special Raspberry Pi B+ and RPi2 Hat (Hardware attached (on) top)
