# Fritzing sketch Tilt_Switch (saved by Fritzing 0.9.3b)
breadboards: 1

parts:
  S1 = Tilt Switch [package=THT]
  LED1 = LED - 5mm [color="Red (633nm)" package="5 mm [THT]"]
  LED2 = LED - 5mm [color="Green (560nm)" package="5 mm [THT]"]
  R1 = Resistor [tolerance=±5% resistance=220 package=THT]
  R2 = Resistor [tolerance=±5% resistance=220 package=THT]
  Raspberry_Pi_2 = Raspberry Pi 3 [part_number=RPI-3-V1.2]
  R3 = Resistor [tolerance=±5% resistance=10k package=THT]

nets:
  N1: S1.Pin_1, LED1.cathode, LED2.cathode, Raspberry_Pi_2.GND
  N2: S1.Pin_2, Raspberry_Pi_2.GPIO17, R3.Pin_1
  N3: LED1.anode, R2.Pin_0
  N4: LED2.anode, R1.Pin_0
  N5: R1.Pin_1, Raspberry_Pi_2.GPIO27
  N6: R2.Pin_1, Raspberry_Pi_2.GPIO22
  N7: Raspberry_Pi_2.3v3, R3.Pin_0

custom parts:
  Raspberry Pi 3: The RPi3, a faster version of the awesome Raspberry Pi 2 B ARM Board with 40 pin gpio. Ready for special Raspberry Pi B+ and RPi2 Hat (Hardware attached (on) top)
