# Fritzing sketch TrafficLight (saved by Fritzing 0.9.3b)
breadboards: 1

parts:
  IC2 = IC, DIP package, 16 pins [chip_label=74HC595]
  DI1 = 7-Segment LED Display [package=THT]
  LED1 = LED - 5mm [color="Red (633nm)" package="5 mm [THT]"]
  LED2 = LED - 5mm [color="Yellow (595nm)" package="5 mm [THT]"]
  LED3 = LED - 5mm [color="Green (560nm)" package="5 mm [THT]"]
  R1 = Resistor [tolerance=±5% resistance=220 package=THT]
  R2 = Resistor [tolerance=±5% resistance=220 package=THT]
  R3 = Resistor [tolerance=±5% resistance=220 package=THT]
  R4 = Resistor [tolerance=±5% resistance=220 package=THT]
  Raspberry_Pi_2 = Raspberry Pi 3 [part_number=RPI-3-V1.2]

nets:
  N1: IC2.pin1, DI1.cathodeB
  N2: IC2.pin2, DI1.cathodeC
  N3: IC2.pin3, DI1.cathodeD
  N4: IC2.pin4, DI1.cathodeE
  N5: IC2.pin5, DI1.cathodeF
  N6: IC2.pin6, DI1.cathodeG
  N7: IC2.pin7, DI1.cathodeDP
  N8: IC2.pin8, IC2.pin13, R1.Pin_1, R2.Pin_1, R3.Pin_1, R4.Pin_1, Raspberry_Pi_2.GND
  N9: IC2.pin10, IC2.pin16, Raspberry_Pi_2.3v3
  N10: IC2.pin11, Raspberry_Pi_2.GPIO27
  N11: IC2.pin12, Raspberry_Pi_2.GPIO18
  N12: IC2.pin14, Raspberry_Pi_2.GPIO17
  N13: IC2.pin15, DI1.cathodeA
  N14: DI1.commAnode#2, R4.Pin_0
  N15: LED1.cathode, R3.Pin_0
  N16: LED1.anode, Raspberry_Pi_2.GPIO22
  N17: LED2.cathode, R2.Pin_0
  N18: LED2.anode, Raspberry_Pi_2.GPIO24
  N19: LED3.cathode, R1.Pin_0
  N20: LED3.anode, Raspberry_Pi_2.GPIO23

custom parts:
  Raspberry Pi 3: The RPi3, a faster version of the awesome Raspberry Pi 2 B ARM Board with 40 pin gpio. Ready for special Raspberry Pi B+ and RPi2 Hat (Hardware attached (on) top)
