# Fritzing sketch passivebuzzer (saved by Fritzing 0.9.3b)
breadboards: 1

parts:
  S1 = buzzer [package="[THT]"]
  Q1 = NPN-Transistor [package="TO92 [THT]"]
  R1 = Resistor [tolerance=±5% resistance=1k package=THT]
  Raspberry_Pi_2 = Raspberry Pi 3 [part_number=RPI-3-V1.2]

nets:
  N1: S1.GND, Q1.C
  VCC: S1.VCC, Raspberry_Pi_2.5V
  N2: Q1.E, Raspberry_Pi_2.GND
  N3: Q1.B, R1.Pin_0
  N4: R1.Pin_1, Raspberry_Pi_2.GPIO17

custom parts:
  Raspberry Pi 3: The RPi3, a faster version of the awesome Raspberry Pi 2 B ARM Board with 40 pin gpio. Ready for special Raspberry Pi B+ and RPi2 Hat (Hardware attached (on) top)
