# Fritzing sketch relay (saved by Fritzing 0.9.3b)
breadboards: 1

parts:
  Q1 = NPN-Transistor [package="TO92 [THT]"]
  D1 = Rectifier Diode [part_number=1N4001 package="300 mil [THT]"]
  LED1 = LED - 5mm [color="Red (633nm)" package="5 mm [THT]"]
  R3 = Resistor [tolerance=±5% resistance=1k package=THT]
  R2 = Resistor [tolerance=±5% resistance=220 package=THT]
  K1 = Relay [part_number=FRS1B-S package=THT]
  Raspberry_Pi_2 = Raspberry Pi 3 [part_number=RPI-3-V1.2]

nets:
  N1: Q1.E, LED1.cathode, Raspberry_Pi_2.GND
  N2: Q1.B, R3.Pin_0
  N3: Q1.C, D1.anode, K1.COIL1
  N4: D1.cathode, K1.C1, K1.C2, K1.COIL2, Raspberry_Pi_2.5V
  N5: LED1.anode, R2.Pin_0
  N6: R3.Pin_1, Raspberry_Pi_2.GPIO17
  N7: R2.Pin_1, K1.B

custom parts:
  Relay: An SPDT relay.
  Raspberry Pi 3: The RPi3, a faster version of the awesome Raspberry Pi 2 B ARM Board with 40 pin gpio. Ready for special Raspberry Pi B+ and RPi2 Hat (Hardware attached (on) top)
